// Logisim project Project3Given.circ as structural Verilog: 10 circuits, main circuit CPU15
module main (
  input  EnableBreakpoint,
  input  [14:0] Breakpoint
);

  wire and_2_out, and_3_out, chipset_1_irq, CLK, clock_1_out, cpu15_1_c, cpu15_1_e, cpu15_1_i, cpu15_1_n,
       cpu15_1_o, cpu15_1_z, KBCLR, KBIRQ, KBRD, MEMCS, nand_1_out, RE, TTYCLR, TTYWE, undriven, WE;
  wire [6:0] KBDATA, TTYDATA;
  wire [7:0] cpu15_1_srf;
  wire [14:0] ADDR, chipset_1_ivect, chipset_1_led0, chipset_1_led1, chipset_1_led2, chipset_1_led3,
       chipset_1_led4, chipset_1_led5, chipset_1_led6, chipset_1_led7, chipset_1_led8, chipset_1_led9,
       chipset_1_leda, chipset_1_ledb, chipset_1_ledc, chipset_1_ledd, chipset_1_lede, cpu15_1_ib,
       cpu15_1_pc, cpu15_1_r0, cpu15_1_r1, cpu15_1_r2, cpu15_1_r3, cpu15_1_r4, cpu15_1_r5, cpu15_1_r6,
       cpu15_1_r7, cpu15_1_srp, DATA, xnor_1_out;

  Clock clock_1 (.out(clock_1_out));
  nand nand_1 (nand_1_out, EnableBreakpoint, xnor_1_out[0], xnor_1_out[1], xnor_1_out[2], xnor_1_out[3], xnor_1_out[4], xnor_1_out[5], xnor_1_out[6], xnor_1_out[7], xnor_1_out[8], xnor_1_out[9], xnor_1_out[10], xnor_1_out[11], xnor_1_out[12], xnor_1_out[13], xnor_1_out[14], 1'b1);
  and and_1 (CLK, clock_1_out, nand_1_out);
  assign xnor_1_out = ~(Breakpoint ^ cpu15_1_pc);  // XNOR_Gate xnor_1, 15 bits wide
  LED I (.in(cpu15_1_i));
  LED Z (.in(cpu15_1_z));
  LED N (.in(cpu15_1_n));
  LED O (.in(cpu15_1_o));
  LED C (.in(cpu15_1_c));
  LED E (.in(cpu15_1_e));
  and and_2 (and_2_out, WE, MEMCS);
  and and_3 (and_3_out, MEMCS, RE);
  // Probe on undriven
  RAM #(.addrWidth(15), .asyncread("true"), .dataWidth(15), .databus("bidir")) ram_1 (
    .addr(ADDR), .we(and_2_out), .oe(and_3_out), .clk(CLK), .data(DATA));
  // Probe on cpu15_1_pc
  // Probe on cpu15_1_ib
  // Probe on cpu15_1_srp
  // Probe on cpu15_1_srf
  // Probe on cpu15_1_r0
  // Probe on cpu15_1_r1
  // Probe on cpu15_1_r2
  // Probe on cpu15_1_r3
  // Probe on cpu15_1_r4
  // Probe on cpu15_1_r5
  // Probe on cpu15_1_r6
  // Probe on cpu15_1_r7
  CPU15 cpu15_1 (
    .I(cpu15_1_i), .Z(cpu15_1_z), .N(cpu15_1_n), .O(cpu15_1_o), .C(cpu15_1_c), .E(cpu15_1_e),
    .PC(cpu15_1_pc), .IB(cpu15_1_ib), .SRP(cpu15_1_srp), .SRF(cpu15_1_srf), .R0(cpu15_1_r0), .R1(cpu15_1_r1),
    .R2(cpu15_1_r2), .R3(cpu15_1_r3), .R4(cpu15_1_r4), .R5(cpu15_1_r5), .R6(cpu15_1_r6), .R7(cpu15_1_r7),
    .CLK(CLK), .IRQ(chipset_1_irq), .RE(RE), .WE(WE), .ADDR(ADDR), .DATAIN(DATA), .DATAOUT(DATA));
  // Probe on ADDR
  // Probe on DATA
  // Probe on chipset_1_ivect
  // Probe on TTYDATA
  CHIPSET chipset_1 (
    .RE(RE), .WE(WE), .ADDR(ADDR), .CPUDATAIN(DATA), .CPUDATAOUT(DATA), .IRQ(chipset_1_irq),
    .IVECT(chipset_1_ivect), .CLK(CLK), .MEMCS(MEMCS), .TTYWR(TTYWE), .TTYCLR(TTYCLR), .TTYDATA(TTYDATA),
    .KBRD(KBRD), .KBCLR(KBCLR), .KBIRQ(KBIRQ), .KBDATA(KBDATA), .LED0(chipset_1_led0), .LED1(chipset_1_led1),
    .LED2(chipset_1_led2), .LED3(chipset_1_led3), .LED4(chipset_1_led4), .LED5(chipset_1_led5),
    .LED6(chipset_1_led6), .LED7(chipset_1_led7), .LED8(chipset_1_led8), .LED9(chipset_1_led9),
    .LEDA(chipset_1_leda), .LEDB(chipset_1_ledb), .LEDC(chipset_1_ledc), .LEDD(chipset_1_ledd),
    .LEDE(chipset_1_lede));
  TTY tty_1 (.data(TTYDATA), .clk(CLK), .we(TTYWE), .clr(TTYCLR));
  Keyboard keyboard_1 (.clk(CLK), .re(KBRD), .clr(KBCLR), .avail(KBIRQ), .data(KBDATA));
  DotMatrix #(.matrixcols(15), .matrixrows(15)) dotmatrix_1 (
    .col0(chipset_1_led0), .col1(chipset_1_led1), .col2(chipset_1_led2), .col3(chipset_1_led3),
    .col4(chipset_1_led4), .col5(chipset_1_led5), .col6(chipset_1_led6), .col7(chipset_1_led7),
    .col8(chipset_1_led8), .col9(chipset_1_led9), .col10(chipset_1_leda), .col11(chipset_1_ledb),
    .col12(chipset_1_ledc), .col13(chipset_1_ledd), .col14(chipset_1_lede));
endmodule

// CPU
module CPU15 (
  input  [14:0] DATAIN,
  input  CLK,
  input  IRQ,
  output [14:0] PC,
  output [14:0] IB,
  output [14:0] SRP,
  output [7:0] SRF,
  output [14:0] R0,
  output [14:0] R1,
  output [14:0] R2,
  output [14:0] R3,
  output [14:0] R4,
  output [14:0] R5,
  output [14:0] R6,
  output [14:0] R7,
  output RE,
  output WE,
  output I,
  output Z,
  output [14:0] ADDR,
  output N,
  output O,
  output C,
  output E,
  output [14:0] DATAOUT
);

  wire and_1_out, and_2_out, and_4_out, BCF, BNCF, BNF, BNNF, BNZF, BZF, CF, FETCH, JAL, JALR, LOADPC, LW,
       or_2_out, REGW, SW, SWI, WRITEBACK;
  wire [1:0] ASEL, BSEL, FLAGSRC;
  wire [2:0] ALUOP, REGDATASRC;
  wire [3:0] NF;
  wire [7:0] FLAGWM, undriven;
  wire [7:4] flags8_1_f;
  wire [14:0] A, adder15_1_s, ALURES, B, imm15_1_sext, imm15_2_sext, imm15_3_sext, multiplexer_2_out,
       multiplexer_3_out, multiplexer_4_out, multiplexer_5_out;

  T_Flip_Flop t_ff_1 (.T(1'b1), .clk(CLK), .Q(WRITEBACK), .Qn(FETCH));  // open: reset, preset
  Multiplexer #(.width(15)) multiplexer_1 (.in0(ALURES), .in1(PC), .out(ADDR), .sel(FETCH));
  and and_1 (and_1_out, LOADPC, WRITEBACK);
  Counter #(.max('h7fff), .width(15)) PROGRAMCOUNTER (
    .load(and_1_out), .up(1'b1), .count(WRITEBACK), .clk(CLK), .D(ALURES), .Q(PC));  // open: clr, carry
  or or_1 (RE, FETCH, and_2_out);
  and and_2 (and_2_out, LW, ~SW);  // AND_Gate
  and and_3 (WE, WRITEBACK, SW);
  assign DATAOUT = WE ? B : 15'bz;  // Controlled_Buffer controlled_buffer_1
  or or_2 (or_2_out, FETCH, LW);
  ADDER15 adder15_1 (.A(PC), .B(15'h1), .S(adder15_1_s));  // open: CIN, COUT
  Register #(.width(15)) InstructionBuffer (.D(DATAIN), .en(or_2_out), .Q(IB), .clk(CLK));  // open: clr
  IMM15 imm15_1 (.INST(IB), .SEXT(imm15_1_sext));
  Multiplexer #(.select(3), .width(15)) multiplexer_2 (
    .in0(ALURES), .in1(adder15_1_s), .in2(DATAIN), .in3(imm15_1_sext), .out(multiplexer_2_out),
    .sel(REGDATASRC));  // open: in4, in5, in6, in7
  DECODE15 decode15_1 (
    .OPCODE(IB[4:0]), .SWI(SWI), .STORE(SW), .LOAD(LW), .ASEL(ASEL), .BSEL(BSEL), .ALUOP(ALUOP),
    .REGDATASRC(REGDATASRC), .REGW(REGW), .FLAGSRC(FLAGSRC), .FLAGWM(FLAGWM));  // open: SRPW, SRFW
  and and_4 (and_4_out, REGW, WRITEBACK);
  and and_5 (BNZF, IB[4], ~IB[3], ~IB[2], ~IB[1], IB[0], ~Z);  // AND_Gate
  and and_6 (BNF, IB[4], ~IB[3], ~IB[2], IB[1], ~IB[0], N);  // AND_Gate
  and and_7 (BZF, IB[4], ~IB[3], ~IB[2], ~IB[1], ~IB[0], Z);  // AND_Gate
  and and_8 (BCF, IB[4], ~IB[3], IB[2], ~IB[1], ~IB[0], C);  // AND_Gate
  and and_9 (BNCF, IB[4], ~IB[3], IB[2], ~IB[1], IB[0], ~C);  // AND_Gate
  and and_10 (JAL, IB[4], IB[3], IB[2], ~IB[1], ~IB[0]);  // AND_Gate
  and and_11 (JALR, IB[4], IB[3], ~IB[2], IB[1], IB[0]);  // AND_Gate
  Multiplexer #(.select(3), .width(15)) multiplexer_3 (
    .in0(R0), .in1(R1), .in2(R2), .in3(R3), .in4(R4), .in5(R5), .in6(R6), .in7(R7), .out(multiplexer_3_out),
    .sel(IB[13:11]));
  and and_12 (BNNF, IB[4], ~IB[3], ~IB[2], IB[1], IB[0], ~N);  // AND_Gate
  REGS15 regs15_1 (
    .D(multiplexer_2_out), .W(and_4_out), .SelD(IB[7:5]), .CLK(CLK), .SelA(IB[10:8]), .SelB(IB[13:11]),
    .R0(R0), .R1(R1), .R2(R2), .R3(R3), .R4(R4), .R5(R5), .R6(R6), .R7(R7), .A(A), .B(B));
  IMM15 imm15_2 (.INST(IB), .SEXT(imm15_2_sext));
  or or_3 (LOADPC, BZF, BNZF, BNF, BNNF, BCF, BNCF, JAL, JALR);
  Multiplexer #(.select(2), .width(15)) multiplexer_4 (
    .in0(A), .in1(PC), .out(multiplexer_4_out), .sel(ASEL));  // open: in2, in3
  Multiplexer #(.select(2), .width(15)) multiplexer_5 (
    .in0(B), .in1(imm15_2_sext), .out(multiplexer_5_out), .sel(BSEL));  // open: in2, in3
  ALU15 alu15_1 (
    .A(multiplexer_4_out), .B(multiplexer_5_out), .OP(ALUOP), .CIN(C), .OIN(O), .R(ALURES), .C(CF),
    .O(NF[3]), .N(NF[1]), .Z(NF[0]));
  IMM15 imm15_3 (.INST(IB), .SEXT(imm15_3_sext));
  Multiplexer #(.select(2), .width(8)) multiplexer_6 (
    .in0({1'b0, E, I, 1'b0, NF[3], CF, NF[1:0]}), .in1(A[7:0]), .in2(imm15_3_sext[7:0]), .sel(FLAGSRC));  // open: in3, out
  FLAGS8 flags8_1 (
    .NF(undriven), .WM(FLAGWM), .CLK(CLK), .F({flags8_1_f[7], I, E, flags8_1_f[4], O, C, N, Z}));  // open: IRQ
  // also tied to GND on the sheet: {E, I}

  // Other names for the same wires on the sheet: NF (some bits) = {E, I, CF}; DATA[14:0] = DATAIN; Zflag = NF[0];
  //   Nflag = NF[1]; Oflag = NF[3]; OPCODE[4:0] = IB[4:0]; RD[2:0] = IB[7:5]; RS1[2:0] = IB[10:8];
  //   RS2[2:0] = IB[13:11]
endmodule

module CHIPSET (
  input  RE,
  input  WE,
  input  [14:0] ADDR,
  input  [14:0] CPUDATAIN,
  input  KBIRQ,
  input  [6:0] KBDATA,
  input  CLK,
  output MEMCS,
  output TTYWR,
  output [14:0] IVECT,
  output TTYCLR,
  output [6:0] TTYDATA,
  output KBRD,
  output KBCLR,
  output [14:0] CPUDATAOUT,
  output IRQ,
  output [14:0] LED0,
  output [14:0] LED1,
  output [14:0] LED2,
  output [14:0] LED3,
  output [14:0] LED4,
  output [14:0] LED5,
  output [14:0] LED6,
  output [14:0] LED7,
  output [14:0] LED8,
  output [14:0] LED9,
  output [14:0] LEDA,
  output [14:0] LEDB,
  output [14:0] LEDC,
  output [14:0] LEDD,
  output [14:0] LEDE
);

  wire and_1_out, and_8_out, and_10_out, DATA7, IOCS, IVECTADDR, IVECTEN, IVECTRE, KBCS, LED0EN, LED0END,
       LED1EN, LED1END, LED2EN, LED2END, LED3EN, LED3END, LED4EN, LED4END, LED5EN, LED5END, LED6EN, LED6END,
       LED7EN, LED7END, LED8EN, LED8END, LED9EN, LED9END, LEDAEN, LEDAEND, LEDBEN, LEDBEND, LEDCEN, LEDCEND,
       LEDCS, LEDDEN, LEDDEND, LEDEEN, LEDEEND, LEDFEND, LEDRE, multiplexer_17_out, multiplexer_18_out, RWE,
       TTYCS;
  wire [14:0] DATAL0, DATAL1, DATAL2, DATAL3, DATAL4, DATAL5, DATAL6, DATAL7, DATAL8, DATAL9, DATALA, DATALB,
       DATALC, DATALD, DATALE, LEDDATA;
  wire [14:8] KBDATA15;

  assign CPUDATAOUT = KBRD ? {KBDATA15, DATA7, KBDATA} : 15'bz;  // Controlled_Buffer controlled_buffer_1
  assign CPUDATAOUT = LEDRE ? LEDDATA : 15'bz;  // Controlled_Buffer controlled_buffer_2
  assign CPUDATAOUT = IVECTRE ? IVECT : 15'bz;  // Controlled_Buffer controlled_buffer_3
  Register #(.width(15)) register_1 (.D(DATAL0), .en(LED0EN), .Q(LED0), .clk(CLK));  // open: clr
  Register #(.width(15)) register_2 (.D(DATAL1), .en(LED1EN), .Q(LED1), .clk(CLK));  // open: clr
  Register #(.width(15)) register_3 (.D(DATAL2), .en(LED2EN), .Q(LED2), .clk(CLK));  // open: clr
  Register #(.width(15)) register_4 (.D(DATAL3), .en(LED3EN), .Q(LED3), .clk(CLK));  // open: clr
  Register #(.width(15)) register_5 (.D(DATAL4), .en(LED4EN), .Q(LED4), .clk(CLK));  // open: clr
  and and_1 (and_1_out, WE, LEDCS);
  Decoder #(.select(4)) decoder_1 (
    .out0(LED0END), .out1(LED1END), .out2(LED2END), .out3(LED3END), .out4(LED4END), .out5(LED5END),
    .out6(LED6END), .out7(LED7END), .out8(LED8END), .out9(LED9END), .out10(LEDAEND), .out11(LEDBEND),
    .out12(LEDCEND), .out13(LEDDEND), .out14(LEDEEND), .out15(LEDFEND), .sel(ADDR[3:0]), .en(and_1_out));
  Register #(.width(15)) register_6 (.D(DATAL5), .en(LED5EN), .Q(LED5), .clk(CLK));  // open: clr
  Register #(.width(15)) register_7 (.D(DATAL6), .en(LED6EN), .Q(LED6), .clk(CLK));  // open: clr
  Register #(.width(15)) register_8 (.D(DATAL7), .en(LED7EN), .Q(LED7), .clk(CLK));  // open: clr
  Register #(.width(15)) register_9 (.D(DATAL8), .en(LED8EN), .Q(LED8), .clk(CLK));  // open: clr
  Register #(.width(15)) register_10 (.D(DATAL9), .en(LED9EN), .Q(LED9), .clk(CLK));  // open: clr
  or or_1 (LED0EN, LED0END, LEDFEND);
  or or_2 (LED1EN, LED1END, LEDFEND);
  or or_3 (LED2EN, LED2END, LEDFEND);
  or or_4 (LED3EN, LED3END, LEDFEND);
  or or_5 (LED4EN, LED4END, LEDFEND);
  or or_6 (LED5EN, LED5END, LEDFEND);
  or or_7 (LED6EN, LED6END, LEDFEND);
  or or_8 (LED7EN, LED7END, LEDFEND);
  or or_9 (LED8EN, LED8END, LEDFEND);
  or or_10 (LED9EN, LED9END, LEDFEND);
  or or_11 (LEDAEN, LEDAEND, LEDFEND);
  or or_12 (LEDBEN, LEDBEND, LEDFEND);
  or or_13 (LEDCEN, LEDCEND, LEDFEND);
  or or_14 (LEDDEN, LEDDEND, LEDFEND);
  or or_15 (LEDEEN, LEDEEND, LEDFEND);
  Pull_Resistor pull_resistor_1 (.node(KBDATA15[14]));
  Pull_Resistor pull_resistor_2 (.node(KBDATA15[13]));
  Pull_Resistor pull_resistor_3 (.node(KBDATA15[12]));
  Pull_Resistor pull_resistor_4 (.node(KBDATA15[11]));
  Pull_Resistor pull_resistor_5 (.node(KBDATA15[10]));
  Pull_Resistor pull_resistor_6 (.node(KBDATA15[9]));
  Pull_Resistor pull_resistor_7 (.node(KBDATA15[8]));
  Pull_Resistor pull_resistor_8 (.node(DATA7));
  Register #(.width(15)) register_11 (.D(DATALA), .en(LEDAEN), .Q(LEDA), .clk(CLK));  // open: clr
  Register #(.width(15)) register_12 (.D(DATALB), .en(LEDBEN), .Q(LEDB), .clk(CLK));  // open: clr
  Register #(.width(15)) register_13 (.D(DATALC), .en(LEDCEN), .Q(LEDC), .clk(CLK));  // open: clr
  Register #(.width(15)) register_14 (.D(DATALD), .en(LEDDEN), .Q(LEDD), .clk(CLK));  // open: clr
  Register #(.width(15)) register_15 (.D(DATALE), .en(LEDEEN), .Q(LEDE), .clk(CLK));  // open: clr
  Multiplexer #(.width(15)) multiplexer_1 (.in0(CPUDATAIN), .in1(LED1), .out(DATAL0), .sel(LEDFEND));
  Multiplexer #(.width(15)) multiplexer_2 (.in0(CPUDATAIN), .in1(LED2), .out(DATAL1), .sel(LEDFEND));
  Multiplexer #(.width(15)) multiplexer_3 (.in0(CPUDATAIN), .in1(LED3), .out(DATAL2), .sel(LEDFEND));
  Multiplexer #(.width(15)) multiplexer_4 (.in0(CPUDATAIN), .in1(LED4), .out(DATAL3), .sel(LEDFEND));
  Multiplexer #(.width(15)) multiplexer_5 (.in0(CPUDATAIN), .in1(LED5), .out(DATAL4), .sel(LEDFEND));
  Multiplexer #(.select(4), .width(15)) multiplexer_6 (
    .in0(LED0), .in1(LED1), .in2(LED2), .in3(LED3), .in4(LED4), .in5(LED5), .in6(LED6), .in7(LED7),
    .in8(LED8), .in9(LED9), .in10(LEDA), .in11(LEDB), .in12(LEDC), .in13(LEDD), .in14(LEDE),
    .in15({15{1'b0}}), .out(LEDDATA), .sel(ADDR[3:0]));
  Multiplexer #(.width(15)) multiplexer_7 (.in0(CPUDATAIN), .in1(LED6), .out(DATAL5), .sel(LEDFEND));
  Multiplexer #(.width(15)) multiplexer_8 (.in0(CPUDATAIN), .in1(LED7), .out(DATAL6), .sel(LEDFEND));
  Multiplexer #(.width(15)) multiplexer_9 (.in0(CPUDATAIN), .in1(LED8), .out(DATAL7), .sel(LEDFEND));
  Multiplexer #(.width(15)) multiplexer_10 (.in0(CPUDATAIN), .in1(LED9), .out(DATAL8), .sel(LEDFEND));
  Multiplexer #(.width(15)) multiplexer_11 (.in0(CPUDATAIN), .in1(LEDA), .out(DATAL9), .sel(LEDFEND));
  and and_2 (LEDRE, RE, LEDCS);
  Multiplexer #(.width(15)) multiplexer_12 (.in0(CPUDATAIN), .in1(LEDB), .out(DATALA), .sel(LEDFEND));
  Multiplexer #(.width(15)) multiplexer_13 (.in0(CPUDATAIN), .in1(LEDC), .out(DATALB), .sel(LEDFEND));
  Multiplexer #(.width(15)) multiplexer_14 (.in0(CPUDATAIN), .in1(LEDD), .out(DATALC), .sel(LEDFEND));
  Multiplexer #(.width(15)) multiplexer_15 (.in0(CPUDATAIN), .in1(LEDE), .out(DATALD), .sel(LEDFEND));
  Multiplexer #(.width(15)) multiplexer_16 (.in0(CPUDATAIN), .in1(CPUDATAIN), .out(DATALE), .sel(LEDFEND));
  and and_3 (IOCS, ADDR[5], ADDR[6], ADDR[7], ADDR[8], ADDR[9], ADDR[10], ADDR[11], ADDR[12], ADDR[13], ADDR[14], 1'b1);
  and and_4 (TTYCS, IOCS, ADDR[0], ~ADDR[1], ~ADDR[2], ~ADDR[3], ADDR[4]);  // AND_Gate
  and and_5 (KBCS, IOCS, ~ADDR[0], ~ADDR[1], ~ADDR[2], ~ADDR[3], ADDR[4]);  // AND_Gate
  and and_6 (IVECTADDR, ADDR[0], ADDR[1], ADDR[2], ADDR[3], ADDR[4], ADDR[5], ADDR[6], ADDR[7], ADDR[8], ADDR[9], ADDR[10], ADDR[11], ADDR[12], ADDR[13], ADDR[14]);
  and and_7 (TTYWR, TTYCS, WE);
  and and_8 (and_8_out, TTYWR, DATA7);
  and and_9 (KBRD, KBCS, RE);
  and and_10 (and_10_out, KBCS, WE);
  Multiplexer multiplexer_17 (.in0(and_10_out), .in1(1'b0), .out(multiplexer_17_out), .sel(KBCLR));
  and and_11 (LEDCS, IOCS, ~ADDR[4], RWE);  // AND_Gate
  and and_12 (IVECTEN, IVECTADDR, WE);
  and and_13 (IVECTRE, IVECTADDR, RE);
  or or_16 (RWE, RE, WE);
  and and_14 (MEMCS, ~IOCS, RWE);  // AND_Gate
  Multiplexer multiplexer_18 (.in0(and_8_out), .in1(1'b0), .out(multiplexer_18_out), .sel(TTYCLR));
  D_Flip_Flop d_ff_1 (.clk(CLK), .D(multiplexer_17_out), .Q(KBCLR));  // open: Qn, preset, reset
  Register #(.width(15)) register_16 (.D(CPUDATAIN), .en(IVECTEN), .Q(IVECT), .clk(CLK));  // open: clr
  D_Flip_Flop d_ff_2 (.clk(CLK), .D(multiplexer_18_out), .Q(TTYCLR));  // open: Qn, preset, reset

  assign IRQ = KBIRQ;
  assign TTYDATA = CPUDATAIN[6:0];

  // Other names for the same wires on the sheet: DATA[14:0] = CPUDATAIN; KBDATA15[7:0] = {DATA7, KBDATA}
endmodule

module ADDER15 (
  input  [14:0] A,
  input  [14:0] B,
  input  CIN,
  output COUT,
  output [14:0] S
);

  wire adder5_2_cout, adder5_3_cout;

  ADDER5 adder5_1 (.Cin(adder5_2_cout), .A(A[14:10]), .B(B[14:10]), .COUT(COUT), .S(S[14:10]));
  ADDER5 adder5_2 (.Cin(adder5_3_cout), .A(A[9:5]), .B(B[9:5]), .COUT(adder5_2_cout), .S(S[9:5]));
  ADDER5 adder5_3 (.Cin(CIN), .A(A[4:0]), .B(B[4:0]), .COUT(adder5_3_cout), .S(S[4:0]));
endmodule

module REGS15 (
  input  [14:0] D,
  input  W,
  input  [2:0] SelD,
  input  CLK,
  input  [2:0] SelA,
  input  [2:0] SelB,
  output [14:0] R0,
  output [14:0] R1,
  output [14:0] R2,
  output [14:0] R3,
  output [14:0] R4,
  output [14:0] R5,
  output [14:0] R6,
  output [14:0] R7,
  output [14:0] A,
  output [14:0] B
);

  wire demultiplexer_1_out0, demultiplexer_1_out1, demultiplexer_1_out2, demultiplexer_1_out3,
       demultiplexer_1_out4, demultiplexer_1_out5, demultiplexer_1_out6, demultiplexer_1_out7;

  Demultiplexer #(.select(3)) demultiplexer_1 (
    .out0(demultiplexer_1_out0), .out1(demultiplexer_1_out1), .out2(demultiplexer_1_out2),
    .out3(demultiplexer_1_out3), .out4(demultiplexer_1_out4), .out5(demultiplexer_1_out5),
    .out6(demultiplexer_1_out6), .out7(demultiplexer_1_out7), .in(W), .sel(SelD));
  Register #(.width(15)) register_1 (.D({15{1'b0}}), .en(demultiplexer_1_out0), .Q(R0), .clk(CLK));  // open: clr
  Register #(.width(15)) register_2 (.D(D), .en(demultiplexer_1_out1), .Q(R1), .clk(CLK));  // open: clr
  Register #(.width(15)) register_3 (.D(D), .en(demultiplexer_1_out2), .Q(R2), .clk(CLK));  // open: clr
  Register #(.width(15)) register_4 (.D(D), .en(demultiplexer_1_out3), .Q(R3), .clk(CLK));  // open: clr
  Register #(.width(15)) register_5 (.D(D), .en(demultiplexer_1_out4), .Q(R4), .clk(CLK));  // open: clr
  Register #(.width(15)) register_6 (.D(D), .en(demultiplexer_1_out5), .Q(R5), .clk(CLK));  // open: clr
  Register #(.width(15)) register_7 (.D(D), .en(demultiplexer_1_out6), .Q(R6), .clk(CLK));  // open: clr
  Register #(.width(15)) register_8 (.D(D), .en(demultiplexer_1_out7), .Q(R7), .clk(CLK));  // open: clr
  Multiplexer #(.select(3), .width(15)) multiplexer_1 (
    .in0(R0), .in1(R1), .in2(R2), .in3(R3), .in4(R4), .in5(R5), .in6(R6), .in7(R7), .out(A), .sel(SelA));
  Multiplexer #(.select(3), .width(15)) multiplexer_2 (
    .in0(R0), .in1(R1), .in2(R2), .in3(R3), .in4(R4), .in5(R5), .in6(R6), .in7(R7), .out(B), .sel(SelB));
endmodule

module ALU15 (
  input  [14:0] A,
  input  [14:0] B,
  input  [2:0] OP,
  input  CIN,
  input  OIN,
  output C,
  output O,
  output N,
  output Z,
  output [14:0] R
);

  wire and_3_out, and_4_out, and_5_out, and_6_out, Cdif, Csll, Csra, Csrl, Csum, msbB2, msbDIF,
       multiplexer_4_out, multiplexer_5_out, multiplexer_7_out, multiplexer_9_out, multiplexer_12_out,
       multiplexer_13_out, multiplexer_20_out, multiplexer_22_out, multiplexer_24_out, or_2_out, or_3_out;
  wire [13:0] adder15_2_s, SUB;
  wire [14:0] ADD, AND1, multiplexer_2_out, multiplexer_3_out, multiplexer_6_out, multiplexer_8_out,
       multiplexer_10_out, multiplexer_11_out, multiplexer_19_out, multiplexer_21_out, multiplexer_23_out,
       not_1_out, OR1, SLL1, SRA1, SRL1, XOR1;

  Multiplexer #(.select(3), .width(15)) multiplexer_1 (
    .in0(ADD), .in1({msbDIF, SUB}), .in2(AND1), .in3(OR1), .in4(XOR1), .in5(SLL1), .in6(SRL1), .in7(SRA1),
    .out({N, R[13:0]}), .sel(OP));
  and and_1 (Z, ~R[0], ~R[1], ~R[2], ~R[3], ~R[4], ~R[5], ~R[6], ~R[7], ~R[8], ~R[9], ~R[10], ~R[11], ~R[12], ~R[13], ~N);  // AND_Gate
  assign AND1 = A & B;  // AND_Gate and_2, 15 bits wide
  Multiplexer #(.width(15)) multiplexer_2 (.in0(A), .in1({A[13:0], 1'b0}), .out(multiplexer_2_out), .sel(B[0]));
  Multiplexer #(.width(15)) multiplexer_3 (.in0(A), .in1({1'b0, A[14:1]}), .out(multiplexer_3_out), .sel(B[0]));
  assign OR1 = A | B;  // OR_Gate or_1, 15 bits wide
  Multiplexer multiplexer_4 (.in0(1'b0), .in1(A[14]), .out(multiplexer_4_out), .sel(B[0]));
  Multiplexer multiplexer_5 (.in0(1'b0), .in1(A[0]), .out(multiplexer_5_out), .sel(B[0]));
  ADDER15 adder15_1 (.A(A), .B({msbB2, adder15_2_s}), .COUT(Cdif), .S({msbDIF, SUB}));  // open: CIN
  assign XOR1 = A ^ B;  // XOR_Gate xor_1, 15 bits wide
  Multiplexer #(.width(15)) multiplexer_6 (
    .in0(multiplexer_2_out), .in1({multiplexer_2_out[12:0], 2'b00}), .out(multiplexer_6_out), .sel(B[1]));
  Multiplexer multiplexer_7 (.in0(multiplexer_4_out), .in1(multiplexer_2_out[13]), .out(multiplexer_7_out), .sel(B[1]));
  Multiplexer #(.width(15)) multiplexer_8 (
    .in0(multiplexer_3_out), .in1({2'b00, multiplexer_3_out[14:2]}), .out(multiplexer_8_out), .sel(B[1]));
  Multiplexer multiplexer_9 (.in0(multiplexer_5_out), .in1(multiplexer_3_out[1]), .out(multiplexer_9_out), .sel(B[1]));
  assign not_1_out = ~B;  // NOT_Gate not_1, 15 bits wide
  ADDER15 adder15_2 (.A(15'h1), .B(not_1_out), .S({msbB2, adder15_2_s}));  // open: CIN, COUT
  Multiplexer #(.width(15)) multiplexer_10 (
    .in0(multiplexer_6_out), .in1({multiplexer_6_out[10:0], 4'b0000}), .out(multiplexer_10_out), .sel(B[2]));
  Multiplexer #(.width(15)) multiplexer_11 (
    .in0(multiplexer_8_out), .in1({4'b0000, multiplexer_8_out[14:4]}), .out(multiplexer_11_out), .sel(B[2]));
  Multiplexer multiplexer_12 (
    .in0(multiplexer_7_out), .in1(multiplexer_6_out[11]), .out(multiplexer_12_out), .sel(B[2]));
  Multiplexer multiplexer_13 (
    .in0(multiplexer_9_out), .in1(multiplexer_8_out[3]), .out(multiplexer_13_out), .sel(B[2]));
  ADDER15 adder15_3 (.A(A), .B(B), .CIN(CIN), .COUT(Csum), .S(ADD));
  Multiplexer #(.width(15)) multiplexer_14 (
    .in0(multiplexer_10_out), .in1({multiplexer_10_out[6:0], {8{1'b0}}}), .out(SLL1), .sel(B[3]));
  Multiplexer #(.width(15)) multiplexer_15 (
    .in0(multiplexer_11_out), .in1({{8{1'b0}}, multiplexer_11_out[14:8]}), .out(SRL1), .sel(B[3]));
  Multiplexer multiplexer_16 (.in0(multiplexer_13_out), .in1(multiplexer_11_out[7]), .out(Csrl), .sel(B[3]));
  Multiplexer multiplexer_17 (.in0(multiplexer_12_out), .in1(multiplexer_10_out[7]), .out(Csll), .sel(B[3]));
  and and_3 (and_3_out, A[14], B[14], ~ADD[14]);  // AND_Gate
  and and_4 (and_4_out, ~A[14], ~B[14], ADD[14]);  // AND_Gate
  and and_5 (and_5_out, msbDIF, ~msbB2, ~A[14]);  // AND_Gate
  and and_6 (and_6_out, ~msbDIF, msbB2, A[14]);  // AND_Gate
  or or_2 (or_2_out, and_3_out, and_4_out);
  or or_3 (or_3_out, and_5_out, and_6_out);
  Multiplexer #(.select(3)) multiplexer_18 (
    .in0(Csum), .in1(Cdif), .in2(CIN), .in3(CIN), .in4(CIN), .in5(Csll), .in6(Csrl), .in7(Csra), .out(C),
    .sel(OP));
  Multiplexer #(.width(15)) multiplexer_19 (.in0(A), .in1({{2{A[14]}}, A[13:1]}), .out(multiplexer_19_out), .sel(B[0]));
  Multiplexer multiplexer_20 (.in0(1'b0), .in1(A[0]), .out(multiplexer_20_out), .sel(B[0]));
  or or_4 (O, or_2_out, OIN, or_3_out);
  Multiplexer #(.width(15)) multiplexer_21 (
    .in0(multiplexer_19_out), .in1({{2{A[14]}}, multiplexer_19_out[14:2]}), .out(multiplexer_21_out),
    .sel(B[1]));
  Multiplexer multiplexer_22 (
    .in0(multiplexer_20_out), .in1(multiplexer_19_out[1]), .out(multiplexer_22_out), .sel(B[1]));
  Multiplexer #(.width(15)) multiplexer_23 (
    .in0(multiplexer_21_out), .in1({{4{A[14]}}, multiplexer_21_out[14:4]}), .out(multiplexer_23_out),
    .sel(B[2]));
  Multiplexer multiplexer_24 (
    .in0(multiplexer_22_out), .in1(multiplexer_21_out[3]), .out(multiplexer_24_out), .sel(B[2]));
  Multiplexer #(.width(15)) multiplexer_25 (
    .in0(multiplexer_23_out), .in1({{8{A[14]}}, multiplexer_23_out[14:8]}), .out(SRA1), .sel(B[3]));
  Multiplexer multiplexer_26 (.in0(multiplexer_24_out), .in1(multiplexer_23_out[7]), .out(Csra), .sel(B[3]));

  assign R[14] = N;

  // Other names for the same wires on the sheet: msbA = A[14]; msbA2 = A[14]; msbSUM = ADD[14]; msbB = B[14];
  //   Cslli = Csll; SUB[14] = msbDIF
endmodule

module FLAGS8 (
  input  IRQ,
  input  [7:0] NF,
  input  [7:0] WM,
  input  CLK,
  output [7:0] F
);

  Register #(.width(1)) register_1 (.D(NF[0]), .en(WM[0]), .Q(F[0]), .clk(CLK));  // open: clr
  Register #(.width(1)) register_2 (.D(NF[1]), .en(WM[1]), .Q(F[1]), .clk(CLK));  // open: clr
  Register #(.width(1)) register_3 (.D(NF[2]), .en(WM[2]), .Q(F[2]), .clk(CLK));  // open: clr
  Register #(.width(1)) register_4 (.D(NF[3]), .en(WM[3]), .Q(F[3]), .clk(CLK));  // open: clr
  Register #(.width(1)) register_5 (.D(NF[5]), .en(WM[5]), .Q(F[5]), .clk(CLK));  // open: clr
  Register #(.width(1)) register_6 (.D(NF[6]), .en(WM[6]), .Q(F[6]), .clk(CLK));  // open: clr

  assign {F[7], F[4]} = 2'b00;
endmodule

module IMM15 (
  input  [14:0] INST,
  output [14:0] SEXT
);

  wire [14:0] Four;

  Multiplexer #(.select(2), .width(15)) multiplexer_1 (
    .in0({15{1'b0}}), .in1({{12{INST[14]}}, INST[13:11]}), .in2({{7{INST[14]}}, INST[13:6]}), .in3(Four),
    .out(SEXT), .sel(INST[4:3]));
  Multiplexer #(.select(3), .width(15)) multiplexer_2 (
    .in0({15{1'b0}}), .in1({15{1'b0}}), .in2({15{1'b0}}), .in3({{12{INST[14]}}, INST[13:11]}),
    .in4({{9{INST[14]}}, INST[13:8]}), .in5({{9{INST[14]}}, INST[13:8]}), .in6({{12{INST[14]}}, INST[7:5]}),
    .in7({{5{INST[14]}}, INST[13:8], 4'b0000}), .out(Four), .sel(INST[2:0]));

  // Other names for the same wires on the sheet: Three[14:0] = {{7{INST[14]}}, INST[13:6]};
  //   Two[14:0] = {{12{INST[14]}}, INST[13:11]}; OPCODE[4:0] = INST[4:0]; Select2[2:0] = INST[2:0];
  //   Select1[1:0] = INST[4:3]
endmodule

module DECODE15 (
  input  [4:0] OPCODE,
  output SWI,
  output STORE,
  output LOAD,
  output [1:0] ASEL,
  output [1:0] BSEL,
  output [2:0] ALUOP,
  output [2:0] REGDATASRC,
  output REGW,
  output [1:0] FLAGSRC,
  output [7:0] FLAGWM,
  output SRPW,
  output SRFW
);

  ROM #(.addrWidth(5), .dataWidth(2)) rom_1 (.addr(OPCODE), .data(BSEL));
  ROM #(.addrWidth(5), .dataWidth(2)) rom_2 (.addr(OPCODE), .data(ASEL));
  ROM #(.addrWidth(5), .dataWidth(1)) rom_3 (.addr(OPCODE));  // open: data
  ROM #(.addrWidth(5)) rom_4 (.addr(OPCODE), .data(FLAGWM));
  and and_1 (SWI, OPCODE[0], OPCODE[1], OPCODE[2], ~OPCODE[3], OPCODE[4]);  // AND_Gate
  and and_2 (STORE, OPCODE[4], OPCODE[3], OPCODE[2], OPCODE[1], ~OPCODE[0]);  // AND_Gate
  and and_3 (LOAD, ~OPCODE[4], OPCODE[3], ~OPCODE[2], ~OPCODE[1], OPCODE[0]);  // AND_Gate
  ROM #(.addrWidth(5), .dataWidth(3)) rom_5 (.addr(OPCODE), .data(ALUOP));
  ROM #(.addrWidth(5), .dataWidth(3)) rom_6 (.addr(OPCODE), .data(REGDATASRC));
  ROM #(.addrWidth(5), .dataWidth(2)) rom_7 (.addr(OPCODE), .data(FLAGSRC));

  // Notes on the sheet:
  //   contents of rom_1 (hex, n*v repeats v):
  //   8*0 14*1 5*0 1 1 0 1
  //   contents of rom_2 (hex, n*v repeats v):
  //   16*0 6*1 5*0 1 1
  //   contents of rom_3 (hex, n*v repeats v):
  //   16*1 8*0 6*1 0 1
  //   contents of rom_4 (hex, n*v repeats v):
  //   f f 3 3 3 7 7 7 f 0 3 3 3 7 7 7 6*0 ff 20 0 0 ff
  //   contents of rom_5 (hex, n*v repeats v):
  //   0 1 2 3 4 5 6 7 0 0 2 3 4 5 6 7
  //   contents of rom_6 (hex, n*v repeats v):
  //   9*0 2 17*0 1 1 0 0 3
  //   contents of rom_7 (hex, n*v repeats v):
  //   22*0 3 0 0 0 1 0 0 2
endmodule

module ADDER5 (
  input  [4:0] A,
  input  [4:0] B,
  input  Cin,
  output COUT,
  output [4:0] S
);

  wire and_2_out, and_4_out, and_6_out, and_8_out, and_10_out, C1, C2, C3, C4, G0, G1, G2, G3, G4, P0, P1,
       P2, P3, P4;

  and and_1 (G0, A[0], B[0]);
  xor xor_1 (S[0], P0, Cin);
  xor xor_2 (P0, B[0], A[0]);
  and and_2 (and_2_out, P0, Cin);
  or or_1 (C1, G0, and_2_out);
  and and_3 (G1, A[1], B[1]);
  xor xor_3 (P1, B[1], A[1]);
  and and_4 (and_4_out, P1, C1);
  or or_2 (C2, G1, and_4_out);
  xor xor_4 (S[1], P1, C1);
  and and_5 (G2, A[2], B[2]);
  xor xor_5 (P2, B[2], A[2]);
  and and_6 (and_6_out, P2, C2);
  or or_3 (C3, G2, and_6_out);
  xor xor_6 (S[2], P2, C2);
  and and_7 (G3, A[3], B[3]);
  xor xor_7 (P3, B[3], A[3]);
  and and_8 (and_8_out, P3, C3);
  or or_4 (C4, G3, and_8_out);
  xor xor_8 (S[3], P3, C3);
  and and_9 (G4, A[4], B[4]);
  xor xor_9 (P4, B[4], A[4]);
  and and_10 (and_10_out, P4, C4);
  or or_5 (COUT, G4, and_10_out);
  xor xor_10 (S[4], P4, C4);

  // Other names for the same wires on the sheet: C5 = COUT
endmodule
